# Fritzing sketch arduinoponia (saved by Fritzing 0.9.3b)
breadboards: 1

parts:
  Componente1 = Arduino Uno (Rev3) - ICSP
  LED1 = smd LED [color="Yellow (595nm)" package="0805 [SMD]"]
  LED2 = smd LED [color="Yellow (595nm)" package="0805 [SMD]"]
  LED3 = smd LED [color="Yellow (595nm)" package="0805 [SMD]"]
  R1 = Resistor [tolerance=±5% resistance=470 package=THT]
  R2 = Resistor [tolerance=±5% resistance=470 package=THT]
  R3 = Resistor [tolerance=±5% resistance=470 package=THT]
  R8 = Resistor [tolerance=±5% resistance=10k package="2512 [SMD]"]
  L1 = Inductor [package="400 mil [THT]"]

nets:
  N1: Componente1.A0, R8.Pin_1
  N2: Componente1.D2, R1.Pin_1
  N3: Componente1.D3_PWM, R2.Pin_1
  N4: Componente1.D4, R3.Pin_1
  N5: Componente1.D7, L1.pin_0
  N6: Componente1.GND, LED1.anode, LED2.anode, LED3.anode, R8.Pin_0, L1.pin_1
  N7: LED1.cathode, R1.Pin_0
  N8: LED2.cathode, R2.Pin_0
  N9: LED3.cathode, R3.Pin_0

notes:
  INDICADOR
  SENSOR
  DATA SENSOR
  BOMBA AGUA
